// Logisim project 16-bit CPU.circ as structural Verilog: 8 circuits, main circuit main
module main (
  input  in_1,
  output [15:0] out_2,
  output [15:0] out_3,
  output [15:0] next_instr,
  output [5:0] imm,
  output [15:0] complement
);

  wire ALU_zero, and_1_out, clock_1_out, clock_2_out, control__0, control_alusrc, control_branch,
       control_jump, control_memread, control_memtoreg, control_memwrite, control_regdst, control_regwrite;
  wire [2:0] multiplexer_1_out, splitter_rt;
  wire [3:0] alucontrol_aluopcode, splitter_aluopcode;
  wire [11:6] splitter_rd;
  wire [15:0] adder_1_out, adder_2_out, bit_extender_1_out, multiplexer_2_out, multiplexer_3_out,
       multiplexer_5_out, ram_1_data, register_1_q, rom_1_data, undriven, undriven_2;

  Adder #(.width(16)) adder_1 (.a(next_instr), .b(16'h1), .out(adder_1_out));  // open: cin, cout
  Clock clock_1 (.out(clock_1_out));
  Register #(.width(16)) register_1 (.D(adder_1_out), .en(1'b1), .Q(register_1_q), .clk(clock_1_out));  // open: clr
  ROM #(.addrWidth(16), .dataWidth(16)) rom_1 (.addr(register_1_q), .data(rom_1_data));  // open: sel
  splitter splitter (
    .in_1(rom_1_data), .imm(imm), .rd(splitter_rd[8:6]), .rt(splitter_rt), .rs(splitter_rd[11:9]),
    .aluopcode(splitter_aluopcode));
  Multiplexer #(.width(3), .enable("false")) multiplexer_1 (
    .in0(splitter_rd[8:6]), .in1(splitter_rt), .out(multiplexer_1_out), .sel(control_regdst));
  assign bit_extender_1_out = {{4{splitter_rd[11]}}, {splitter_rd, imm}};  // Bit_Extender bit_extender_1
  Control control (
    .opcode(splitter_aluopcode), .RegDst(control_regdst), .Jump(control_jump), .Branch(control_branch),
    .MemRead(control_memread), .MemToReg(control_memtoreg), .MemWrite(control_memwrite),
    .ALUSrc(control_alusrc), .RegWrite(control_regwrite), ._0(control__0));
  assign complement = {{10{imm[5]}}, imm};  // Bit_Extender bit_extender_2
  register_file Register_file (
    .Write(control_regwrite), .Write_Register(multiplexer_1_out), .r0(control__0),
    .Register_Data(multiplexer_5_out), .Clock(clock_1_out), .Reset(in_1), .Read_R2(splitter_rd[11:9]),
    .Read_R1(splitter_rt));  // open: Data1, Data2
  Adder #(.width(16)) adder_2 (.a(bit_extender_1_out), .b(register_1_q), .out(adder_2_out));  // open: cin, cout
  ALU ALU (.i2(multiplexer_2_out), .SelectOp(alucontrol_aluopcode), .Zero(ALU_zero));  // open: i1, ALU_Output
  Multiplexer #(.width(16), .enable("false")) multiplexer_2 (
    .in0(undriven), .in1(complement), .out(multiplexer_2_out), .sel(control_alusrc));
  alucontrol alucontrol (.funct(imm[2:0]), .opcode(splitter_aluopcode), .ALUOpcode(alucontrol_aluopcode));
  Adder #(.width(16)) adder_3 (.a(register_1_q), .b(complement), .out(out_2));  // open: cin, cout
  and and_1 (and_1_out, control_branch, ALU_zero);
  Clock clock_2 (.out(clock_2_out));
  Multiplexer #(.width(16), .enable("false")) multiplexer_3 (
    .in0(register_1_q), .in1(out_2), .out(multiplexer_3_out), .sel(and_1_out));
  RAM #(.addrWidth(16), .dataWidth(16), .bus("separate")) ram_1 (
    .addr(undriven_2), .din(undriven), .data(ram_1_data), .str(control_memwrite), .clk(clock_2_out),
    .ld(control_memread));  // open: sel, clr
  Multiplexer #(.width(16), .enable("false")) multiplexer_4 (
    .in0(multiplexer_3_out), .in1(adder_2_out), .out(next_instr), .sel(control_jump));
  Multiplexer #(.width(16), .enable("false")) multiplexer_5 (
    .in0(ram_1_data), .in1(undriven_2), .out(multiplexer_5_out), .sel(control_memtoreg));

  assign out_3 = complement;
endmodule

module register_file (
  input  Write,
  input  [2:0] Write_Register,
  input  r0,
  input  [15:0] Register_Data,
  input  [2:0] Read_R2,
  input  [2:0] Read_R1,
  input  Clock,
  input  Reset,
  output [15:0] Data1,
  output [15:0] Data2
);

  wire and_1_out, and_2_out, and_3_out, and_4_out, and_5_out, and_6_out, and_7_out, and_8_out,
       decoder_1_out0, decoder_1_out1, decoder_1_out2, decoder_1_out3, decoder_1_out4, decoder_1_out5,
       decoder_1_out6, decoder_1_out7, not_1_out;
  wire [15:0] bit_extender_1_out, multiplexer_2_out, r1_q, r2_q, r3_q, r4_q, r5_q, r6_q, r7_q, r8_q;

  Decoder #(.select(3), .enable("false")) decoder_1 (
    .out0(decoder_1_out0), .out1(decoder_1_out1), .out2(decoder_1_out2), .out3(decoder_1_out3),
    .out4(decoder_1_out4), .out5(decoder_1_out5), .out6(decoder_1_out6), .out7(decoder_1_out7),
    .sel(Write_Register));
  and and_1 (and_1_out, Write, decoder_1_out0);
  and and_2 (and_2_out, Write, decoder_1_out1);
  and and_3 (and_3_out, Write, decoder_1_out2);
  and and_4 (and_4_out, Write, decoder_1_out3);
  and and_5 (and_5_out, Write, decoder_1_out4);
  and and_6 (and_6_out, Write, decoder_1_out5);
  and and_7 (and_7_out, Write, decoder_1_out6);
  and and_8 (and_8_out, Write, decoder_1_out7);
  Register #(.width(16)) r1 (.D(Register_Data), .en(and_1_out), .Q(r1_q), .clk(Clock), .clr(Reset));
  Register #(.width(16)) r2 (.D(Register_Data), .en(and_2_out), .Q(r2_q), .clk(Clock), .clr(Reset));
  Register #(.width(16)) r3 (.D(Register_Data), .en(and_3_out), .Q(r3_q), .clk(Clock), .clr(Reset));
  Register #(.width(16)) r4 (.en(and_4_out), .Q(r4_q), .clk(Clock), .clr(Reset));  // open: D
  Register #(.width(16)) r5 (.D(Register_Data), .en(and_5_out), .Q(r5_q), .clk(Clock), .clr(Reset));
  Register #(.width(16)) r6 (.D(Register_Data), .en(and_6_out), .Q(r6_q), .clk(Clock), .clr(Reset));
  Register #(.width(16)) r7 (.D(Register_Data), .en(and_7_out), .Q(r7_q), .clk(Clock), .clr(Reset));
  Register #(.width(16)) r8 (.D(Register_Data), .en(and_8_out), .Q(r8_q), .clk(Clock), .clr(Reset));
  Multiplexer #(.select(3), .width(16), .enable("false")) multiplexer_1 (
    .in0(r1_q), .in1(r2_q), .in2(r3_q), .in3(r4_q), .in4(r5_q), .in5(r6_q), .in6(r7_q), .in7(r8_q),
    .out(Data1), .sel(Read_R1));
  Multiplexer #(.select(3), .width(16)) multiplexer_2 (
    .in0(r1_q), .in1(r2_q), .in2(r3_q), .in3(r4_q), .in4(r5_q), .in5(r6_q), .in6(r7_q), .in7(r8_q),
    .out(multiplexer_2_out), .sel(Read_R2), .en(not_1_out));
  not not_1 (not_1_out, r0);
  Multiplexer #(.width(16), .enable("false")) multiplexer_3 (
    .in0(bit_extender_1_out), .in1(multiplexer_2_out), .out(Data2), .sel(not_1_out));
  assign bit_extender_1_out = {{15{1'b0}}, not_1_out};  // Bit_Extender bit_extender_1
endmodule

module ALU (
  input  [15:0] i1,
  input  [15:0] i2,
  input  [3:0] SelectOp,
  output [15:0] ALU_Output,
  output Zero
);

  wire comparator_1_lt, comparator_2_eq, not_1_out;
  wire [15:0] adder_1_out, and_1_out, bit_extender_1_out, bit_extender_2_out, or_1_out, or_2_out;

  Adder #(.width(16)) adder_1 (.a(i1), .b(i2), .out(adder_1_out));  // open: cin, cout
  assign and_1_out = i1 & i2;  // AND_Gate and_1, 16 bits wide
  assign or_1_out = i2 | i2;  // OR_Gate or_1, 16 bits wide
  assign or_2_out = i2 | {16{1'b0}};  // OR_Gate or_2, 16 bits wide
  Comparator #(.width(16), .mode("unsigned")) comparator_1 (.a(i1), .b(i2), .lt(comparator_1_lt));  // open: gt, eq
  Comparator #(.width(16), .mode("unsigned")) comparator_2 (.a(i1), .b(i2), .eq(comparator_2_eq));  // open: gt, lt
  not not_1 (not_1_out, comparator_2_eq);
  assign bit_extender_1_out = {{15{1'b0}}, comparator_1_lt};  // Bit_Extender bit_extender_1
  assign bit_extender_2_out = {{15{1'b0}}, not_1_out};  // Bit_Extender bit_extender_2
  Multiplexer #(.select(4), .width(16), .enable("false")) multiplexer_1 (
    .in1(or_2_out), .in2(adder_1_out), .in3(and_1_out), .in4(or_1_out), .in5(bit_extender_1_out),
    .in6(bit_extender_2_out), .in7(adder_1_out), .in8(adder_1_out), .in9({16{1'b0}}), .in10({16{1'b0}}),
    .in11({16{1'b0}}), .in12({16{1'b0}}), .in13(adder_1_out), .in14(and_1_out), .in15(or_1_out),
    .out(ALU_Output), .sel(SelectOp));  // open: in0
  not not_2 (Zero, 1'b0);
endmodule

module Control (
  input  [3:0] opcode,
  output RegDst,
  output Jump,
  output Branch,
  output MemRead,
  output MemToReg,
  output MemWrite,
  output ALUSrc,
  output RegWrite,
  output _0
);

  wire and_1_out, and_2_out, and_3_out, and_4_out, and_5_out, and_6_out, and_7_out, and_8_out, and_9_out,
       and_10_out, and_11_out, and_13_out, and_14_out, and_15_out, and_16_out, and_17_out, and_18_out,
       and_19_out, and_20_out, and_21_out, and_22_out, not_1_out, not_2_out, not_3_out, not_4_out, not_5_out,
       not_6_out, not_7_out, not_8_out, not_9_out, not_10_out, not_11_out, not_12_out, not_13_out,
       not_14_out, not_15_out, not_16_out, not_17_out, not_18_out, not_19_out, not_20_out, not_21_out,
       not_22_out, not_23_out, not_24_out, not_25_out, not_26_out, not_27_out, not_28_out, not_29_out,
       not_30_out, not_31_out, not_32_out, not_33_out, not_34_out, not_35_out;

  not not_1 (not_1_out, opcode[2]);
  not not_2 (not_2_out, opcode[1]);
  not not_3 (not_3_out, opcode[0]);
  not not_4 (not_4_out, opcode[2]);
  not not_5 (not_5_out, opcode[2]);
  not not_6 (not_6_out, opcode[3]);
  not not_7 (not_7_out, opcode[1]);
  not not_8 (not_8_out, opcode[2]);
  not not_9 (not_9_out, opcode[3]);
  and and_1 (and_1_out, opcode[2], opcode[0]);
  and and_2 (and_2_out, opcode[2], opcode[1]);
  not not_10 (not_10_out, opcode[2]);
  not not_11 (not_11_out, opcode[1]);
  not not_12 (not_12_out, opcode[0]);
  not not_13 (not_13_out, opcode[2]);
  not not_14 (not_14_out, opcode[3]);
  not not_15 (not_15_out, opcode[2]);
  not not_16 (not_16_out, opcode[1]);
  not not_17 (not_17_out, opcode[3]);
  not not_18 (not_18_out, opcode[3]);
  not not_19 (not_19_out, opcode[1]);
  not not_20 (not_20_out, opcode[0]);
  not not_21 (not_21_out, opcode[2]);
  not not_22 (not_22_out, opcode[1]);
  not not_23 (not_23_out, opcode[3]);
  not not_24 (not_24_out, opcode[2]);
  not not_25 (not_25_out, opcode[3]);
  not not_26 (not_26_out, opcode[1]);
  not not_27 (not_27_out, opcode[0]);
  not not_28 (not_28_out, opcode[3]);
  not not_29 (not_29_out, opcode[3]);
  not not_30 (not_30_out, opcode[2]);
  not not_31 (not_31_out, opcode[1]);
  and and_3 (and_3_out, not_1_out, not_2_out, not_3_out);
  and and_4 (and_4_out, opcode[3], opcode[2], opcode[0]);
  and and_5 (and_5_out, opcode[3], opcode[2], opcode[1]);
  and and_6 (and_6_out, opcode[3], not_4_out, opcode[0]);
  and and_7 (and_7_out, opcode[3], not_5_out, opcode[1]);
  and and_8 (and_8_out, not_6_out, opcode[2], not_7_out, opcode[0]);
  not not_32 (not_32_out, opcode[3]);
  and and_9 (and_9_out, not_32_out, opcode[2], opcode[1], not_33_out);
  not not_33 (not_33_out, opcode[0]);
  not not_34 (not_34_out, opcode[3]);
  and and_10 (and_10_out, not_34_out, opcode[2], opcode[1], opcode[0]);
  and and_11 (and_11_out, opcode[3], not_8_out, opcode[1], not_35_out);
  not not_35 (not_35_out, opcode[0]);
  or or_1 (MemToReg, not_9_out, and_1_out, and_2_out);
  and and_12 (MemWrite, not_10_out, not_11_out, not_12_out);
  and and_13 (and_13_out, not_13_out, opcode[0]);
  and and_14 (and_14_out, not_14_out, not_15_out, not_16_out);
  and and_15 (and_15_out, not_17_out, opcode[1], opcode[0]);
  and and_16 (and_16_out, not_18_out, opcode[2], not_19_out, not_20_out);
  and and_17 (and_17_out, opcode[3], not_21_out, not_22_out);
  and and_18 (and_18_out, not_23_out, not_24_out);
  and and_19 (and_19_out, not_25_out, not_26_out, not_27_out);
  and and_20 (and_20_out, not_28_out, opcode[1], opcode[0]);
  and and_21 (and_21_out, opcode[3], opcode[2], opcode[0]);
  and and_22 (and_22_out, opcode[3], opcode[2], opcode[1]);
  and and_23 (_0, not_29_out, not_30_out, not_31_out, opcode[0]);
  or or_2 (RegDst, and_3_out, and_4_out, and_5_out);
  or or_3 (Jump, and_6_out, and_7_out);
  or or_4 (Branch, and_8_out, and_9_out);
  or or_5 (MemRead, and_10_out, and_11_out);
  or or_6 (ALUSrc, and_13_out, and_14_out, and_15_out, and_16_out, and_17_out);
  or or_7 (RegWrite, and_18_out, and_19_out, and_20_out, and_21_out, and_22_out);
endmodule

module alucontrol (
  input  [2:0] funct,
  input  [3:0] opcode,
  output [3:0] ALUOpcode
);

  wire nor_1_out;
  wire [1:0] not_1_out;

  not not_1 (not_1_out[0], funct[2]);
  nor nor_1 (nor_1_out, opcode[0], opcode[1], opcode[2], opcode[3]);
  or or_1 (not_1_out[1], funct[2], funct[1]);
  Multiplexer #(.width(4), .enable("false")) multiplexer_1 (
    .in0(opcode), .in1({2'b11, not_1_out}), .out(ALUOpcode), .sel(nor_1_out));
endmodule

module Data_Memory (
  input  [15:0] Address,
  input  [15:0] Data_Output,
  input  [15:0] Data_Input,
  input  Write,
  input  Read
);

  wire Clock_out;

  Clock Clock (.out(Clock_out));
  RAM #(.addrWidth(16), .dataWidth(16), .bus("separate")) ram_1 (
    .addr(Address), .din(Data_Input), .data(Data_Output), .str(Write), .clk(Clock_out), .ld(Read));  // open: sel, clr
endmodule

module Instr_memory (
  input  [15:0] in_1,
  output [15:0] Instruction
);

  ROM #(.addrWidth(16), .dataWidth(16)) rom_1 (.addr(in_1), .data(Instruction));  // open: sel

  // Notes on the sheet:
  //   contents of rom_1 (hex, n*v repeats v):
  //   1001 1042 108a 208 52bf 27*0 100 15*0 1000
endmodule

module splitter (
  input  [15:0] in_1,
  output [5:0] imm,
  output [2:0] rd,
  output [2:0] rt,
  output [2:0] rs,
  output [3:0] aluopcode
);


  assign aluopcode = in_1[15:12];
  assign imm = in_1[5:0];
  assign rd = in_1[5:3];
  assign rs = in_1[11:9];
  assign rt = in_1[8:6];
endmodule
